# Fritzing sketch weatherbot (saved by Fritzing 0.9.3b)

parts:
  ESP-01 = ESP8266 WiFi Module [part_number=ESP8266]
  USB_to_UART_FTDI = FTDI_BASIC [package=ftdi_basic]
  DHT-22 = Humidity and Temperature Sensor RHT03
  4xAA = 4 x AAA Battery Mount
  VOLTAGE_REGULATOR = BD10KA5WF-E2 [package=so08wide]

nets:
  N1: ESP-01.RXD, USB_to_UART_FTDI.2
  VCC: ESP-01.VCC, ESP-01.CH_PD, DHT-22.Vcc, VOLTAGE_REGULATOR.OUT
  N2: ESP-01.GPIO_0, DHT-22.Data-signal
  GND: ESP-01.GND, DHT-22.GND_2, VOLTAGE_REGULATOR.GND2
  N3: ESP-01.TXD, USB_to_UART_FTDI.3
  N4: 4xAA.-, VOLTAGE_REGULATOR.GND1
  N5: 4xAA.+, VOLTAGE_REGULATOR.VCC

custom parts:
  ESP8266 WiFi Module: Generic WiFi Module based on the ESP8266 with onboard PCB antenna and UART communications
